// Logisim project 4Bit_CPU.circ as structural Verilog: 15 circuits, main circuit CPU
module CPU (
  input  CLR,
  input  in_2,
  input  in_3
);

  wire clk, DWE, SUB, WE;
  wire [1:0] AFS, RSS;
  wire [2:0] AddrA, AddrB, AddrD, register_file_1_port_a;
  wire [3:0] alu_1_alu_out, multiplexer_1_out, Opcode, register_file_1_port_b;
  wire [3:3] Data, register_file_1_port_a_2;
  wire [7:0] counter_1_q;
  wire [7:7] rom_2_data;
  wire [11:7] rom_1_data;

  Clock u_clk (.out(clk));
  Counter counter_1 (.clr(CLR), .load(in_2), .up(in_3), .count(in_3), .clk(clk), .Q(counter_1_q));  // open: D, carry
  ROM #(.dataWidth(16)) rom_1 (
    .addr(counter_1_q), .data({Opcode, rom_1_data[11], AddrD, rom_1_data[7], AddrA, Data[3], AddrB}));
  // Probe on {Opcode, rom_1_data[11], AddrD, rom_1_data[7], AddrA, Data[3], AddrB}
  // Probe on {Data[3], AddrB}
  // Probe on AddrB
  // Probe on AddrA
  // Probe on AddrD
  // Probe on Opcode
  Multiplexer #(.select(2), .width(4)) multiplexer_1 (
    .in0({Data[3], AddrB}), .in1(alu_1_alu_out), .in2({register_file_1_port_a_2[3], register_file_1_port_a}),
    .out(multiplexer_1_out), .sel(RSS));  // open: in3
  ROM #(.addrWidth(4)) rom_2 (.addr(Opcode), .data({rom_2_data[7], SUB, AFS, RSS, DWE, WE}));
  TTY tty_1 (.data({register_file_1_port_a, register_file_1_port_b}), .clk(clk), .we(DWE), .clr(CLR));
  Register_File register_file_1 (
    .RAddrA(AddrA), .WE(WE), .WAddr(AddrD), .Data_in(multiplexer_1_out), .Clk(clk), .RAddrB(AddrB),
    .Port_A({register_file_1_port_a_2[3], register_file_1_port_a}), .Port_B(register_file_1_port_b));
  // Probe on register_file_1_port_b
  // Probe on alu_1_alu_out
  // Probe on {register_file_1_port_a_2[3], register_file_1_port_a}
  ALU alu_1 (
    .A({register_file_1_port_a_2[3], register_file_1_port_a}), .B(register_file_1_port_b), .sub(SUB),
    .S(AFS), .ALU_OUT(alu_1_alu_out));

  // Other names for the same wires on the sheet: Data[2:0] = AddrB

  // Notes on the sheet:
  //   contents of rom_1 (hex, n*v repeats v):
  //   1000 1106 1202 1303 1404 170a 3047 1701 3017 1703 3017 170f 3017 1702 3017 1700 3027 170c 3047 1701
  //   3017 170d 3017 1702 3017 1700 3027 1702 3073 1701 3037 1705 3037 170a 3007 3034 170b 3027 3033 7634
  //   170d 3037 3036 170a 3007 3034 170a 3027 3032 7644 170d 3037 3036 170a 3007 3034 170d 3027 3032 170d
  //   3037 170f 4527 1101 7651 7646 3036 170a 3007 3034 170d 3027 3032 f642 170d 3037 3036 170a 3007
  //   contents of rom_2 (hex, n*v repeats v):
  //   0 1 9 2 5 15 25 35 7*0 75
endmodule

module Four_bit_register (
  input  [3:0] Din,
  input  Write_EN,
  input  Clk,
  output [3:0] Dout
);

  wire multiplexer_1_out, multiplexer_2_out, multiplexer_3_out, multiplexer_4_out;

  Multiplexer multiplexer_1 (.in0(Dout[0]), .in1(Din[0]), .out(multiplexer_1_out), .sel(Write_EN));
  Multiplexer multiplexer_2 (.in0(Dout[1]), .in1(Din[1]), .out(multiplexer_2_out), .sel(Write_EN));
  Multiplexer multiplexer_3 (.in0(Dout[2]), .in1(Din[2]), .out(multiplexer_3_out), .sel(Write_EN));
  Multiplexer multiplexer_4 (.in0(Dout[3]), .in1(Din[3]), .out(multiplexer_4_out), .sel(Write_EN));
  D_Flip_Flop d_ff_1 (.D(multiplexer_1_out), .clk(Clk), .Q(Dout[0]));  // open: Qn, preset, reset
  D_Flip_Flop d_ff_2 (.D(multiplexer_2_out), .clk(Clk), .Q(Dout[1]));  // open: Qn, preset, reset
  D_Flip_Flop d_ff_3 (.D(multiplexer_3_out), .clk(Clk), .Q(Dout[2]));  // open: Qn, preset, reset
  D_Flip_Flop d_ff_4 (.D(multiplexer_4_out), .clk(Clk), .Q(Dout[3]));  // open: Qn, preset, reset

  // Notes on the sheet:
  //   Jacob Lamb
endmodule

module Register_File (
  input  [2:0] RAddrA,
  input  WE,
  input  [2:0] WAddr,
  input  [3:0] Data_in,
  input  Clk,
  input  [2:0] RAddrB,
  output [3:0] Port_A,
  output [3:0] Port_B
);

  wire decoder_1_out0, decoder_1_out1, decoder_1_out2, decoder_1_out3, decoder_1_out4, decoder_1_out5,
       decoder_1_out6, decoder_1_out7;
  wire [3:0] R0, R1, R2, R3, R4, R5, R6, R7;

  Decoder #(.select(3)) decoder_1 (
    .out0(decoder_1_out0), .out1(decoder_1_out1), .out2(decoder_1_out2), .out3(decoder_1_out3),
    .out4(decoder_1_out4), .out5(decoder_1_out5), .out6(decoder_1_out6), .out7(decoder_1_out7), .sel(WAddr),
    .en(WE));
  Four_bit_register four_bit_register_1 (.Din(Data_in), .Write_EN(decoder_1_out0), .Clk(Clk), .Dout(R0));
  Four_bit_register four_bit_register_2 (.Din(Data_in), .Write_EN(decoder_1_out1), .Clk(Clk), .Dout(R1));
  Four_bit_register four_bit_register_3 (.Din(Data_in), .Write_EN(decoder_1_out2), .Clk(Clk), .Dout(R2));
  Four_bit_register four_bit_register_4 (.Din(Data_in), .Write_EN(decoder_1_out3), .Clk(Clk), .Dout(R3));
  Four_bit_register four_bit_register_5 (.Din(Data_in), .Write_EN(decoder_1_out4), .Clk(Clk), .Dout(R4));
  Four_bit_register four_bit_register_6 (.Din(Data_in), .Write_EN(decoder_1_out5), .Clk(Clk), .Dout(R5));
  Four_bit_register four_bit_register_7 (.Din(Data_in), .Write_EN(decoder_1_out6), .Clk(Clk), .Dout(R6));
  Four_bit_register four_bit_register_8 (.Din(Data_in), .Write_EN(decoder_1_out7), .Clk(Clk), .Dout(R7));
  Multiplexer #(.select(3), .width(4)) multiplexer_1 (
    .in0(R0), .in1(R1), .in2(R2), .in3(R3), .in4(R4), .in5(R5), .in6(R6), .in7(R7), .out(Port_A), .sel(RAddrA));
  Multiplexer #(.select(3), .width(4)) multiplexer_2 (
    .in0(R0), .in1(R1), .in2(R2), .in3(R3), .in4(R4), .in5(R5), .in6(R6), .in7(R7), .out(Port_B), .sel(RAddrB));

  // Notes on the sheet:
  //   Jacob Lamb
endmodule

module MUX2to1_1bit (
  input  A,
  input  S,
  input  B,
  output F
);

  wire and_1_out, and_2_out, not_1_out;

  not not_1 (not_1_out, S);
  and and_1 (and_1_out, A, not_1_out);
  and and_2 (and_2_out, S, B);
  or or_1 (F, and_1_out, and_2_out);
endmodule

module MUX2to1_4bit (
  input  [3:0] A,
  input  [3:0] B,
  input  S,
  output [3:0] F
);

  MUX2to1_1bit mux2to1_1bit_1 (.A(A[3]), .S(S), .B(B[3]), .F(F[3]));
  MUX2to1_1bit mux2to1_1bit_2 (.A(A[2]), .S(S), .B(B[2]), .F(F[2]));
  MUX2to1_1bit mux2to1_1bit_3 (.A(A[1]), .S(S), .B(B[1]), .F(F[1]));
  MUX2to1_1bit mux2to1_1bit_4 (.A(A[0]), .S(S), .B(B[0]), .F(F[0]));
endmodule

module Full_Adder (
  input  A,
  input  B,
  input  Cin,
  output S,
  output Cout
);

  wire and_1_out, and_2_out, and_3_out;

  and and_1 (and_1_out, A, B);
  and and_2 (and_2_out, B, Cin);
  and and_3 (and_3_out, A, Cin);
  xor xor_1 (S, A, B, Cin);
  or or_1 (Cout, and_1_out, and_2_out, and_3_out);
endmodule

module AND_4bit (
  input  [3:0] A,
  input  [3:0] B,
  output [3:0] AND4
);

  and and_1 (AND4[3], A[3], B[3]);
  and and_2 (AND4[2], A[2], B[2]);
  and and_3 (AND4[1], A[1], B[1]);
  and and_4 (AND4[0], A[0], B[0]);
endmodule

module OR_4bit (
  input  [3:0] A,
  input  [3:0] B,
  output [3:0] OR4
);

  or or_1 (OR4[3], A[3], B[3]);
  or or_2 (OR4[2], A[2], B[2]);
  or or_3 (OR4[1], A[1], B[1]);
  or or_4 (OR4[0], A[0], B[0]);
endmodule

module XOR_4bit (
  input  [3:0] A,
  input  [3:0] B,
  output [3:0] XOR4
);

  xor xor_1 (XOR4[0], A[0], B[0]);
  xor xor_2 (XOR4[1], A[1], B[1]);
  xor xor_3 (XOR4[2], A[2], B[2]);
  xor xor_4 (XOR4[3], A[3], B[3]);
endmodule

module MUX4to1_4bit (
  input  [3:0] IN0,
  input  [3:0] IN2,
  input  [3:0] IN1,
  input  [3:0] IN3,
  input  [1:0] S,
  output [3:0] MUX_out
);

  wire [3:0] mux2to1_4bit_1_f, mux2to1_4bit_2_f;

  MUX2to1_4bit mux2to1_4bit_1 (.A(IN0), .B(IN2), .S(S[1]), .F(mux2to1_4bit_1_f));
  MUX2to1_4bit mux2to1_4bit_2 (.A(IN1), .B(IN3), .S(S[1]), .F(mux2to1_4bit_2_f));
  MUX2to1_4bit mux2to1_4bit_3 (.A(mux2to1_4bit_1_f), .B(mux2to1_4bit_2_f), .S(S[0]), .F(MUX_out));

  // Notes on the sheet:
  //   (A input)
  //   (C input)
  //   (B input)
  //   (D input)
  //   Jacob Lamb
  //   (F)
endmodule

module Add_4bit (
  input  [3:0] A,
  input  [3:0] B,
  input  Sub,
  output [3:0] ADD4
);

  wire CO0, CO1, CO2, xor_1_out, xor_2_out, xor_3_out, xor_4_out;

  xor xor_1 (xor_1_out, B[0], Sub);
  xor xor_2 (xor_2_out, B[1], Sub);
  xor xor_3 (xor_3_out, B[2], Sub);
  xor xor_4 (xor_4_out, B[3], Sub);
  Full_Adder full_adder_1 (.A(A[0]), .B(xor_1_out), .Cin(Sub), .S(ADD4[0]), .Cout(CO0));
  Full_Adder full_adder_2 (.A(A[1]), .B(xor_2_out), .Cin(CO0), .S(ADD4[1]), .Cout(CO1));
  Full_Adder full_adder_3 (.A(A[2]), .B(xor_3_out), .Cin(CO1), .S(ADD4[2]), .Cout(CO2));
  Full_Adder full_adder_4 (.A(A[3]), .B(xor_4_out), .Cin(CO2), .S(ADD4[3]));  // open: Cout

  // Other names for the same wires on the sheet: S = Sub

  // Notes on the sheet:
  //   Jacob Lamb
endmodule

module LSR (
  input  [3:0] A,
  output [3:0] LSR4
);


  assign LSR4 = {1'b0, A[3:1]};
endmodule

module LSL (
  input  [3:0] A,
  output [3:0] LSL4
);


  assign LSL4 = {A[2:0], 1'b0};
endmodule

module MUX8to1_4bit (
  input  [3:0] IN0,
  input  [3:0] IN2,
  input  [3:0] IN1,
  input  [3:0] IN3,
  input  [3:0] IN4,
  input  [3:0] IN5,
  input  [3:0] IN6,
  input  [3:0] IN7,
  input  [2:0] S,
  output [3:0] MUX_out
);

  wire [3:0] mux4to1_4bit_1_mux_out, mux4to1_4bit_2_mux_out;

  MUX4to1_4bit mux4to1_4bit_1 (
    .IN0(IN0), .IN2(IN2), .IN1(IN1), .IN3(IN3), .S(S[1:0]), .MUX_out(mux4to1_4bit_1_mux_out));
  MUX4to1_4bit mux4to1_4bit_2 (
    .IN0(IN4), .IN2(IN6), .IN1(IN5), .IN3(IN7), .S(S[1:0]), .MUX_out(mux4to1_4bit_2_mux_out));
  MUX2to1_4bit mux2to1_4bit_1 (.A(mux4to1_4bit_1_mux_out), .B(mux4to1_4bit_2_mux_out), .S(S[2]), .F(MUX_out));

  // Other names for the same wires on the sheet: S01[1:0] = S[1:0]

  // Notes on the sheet:
  //   (F)
endmodule

module ALU (
  input  [3:0] A,
  input  [3:0] B,
  input  sub,
  input  [1:0] S,
  output [3:0] ALU_OUT
);

  wire [3:0] add_4bit_1_add4, and_4bit_1_and4, or_4bit_1_or4, xor_4bit_1_xor4;

  XOR_4bit xor_4bit_1 (.A(A), .B(B), .XOR4(xor_4bit_1_xor4));
  OR_4bit or_4bit_1 (.A(A), .B(B), .OR4(or_4bit_1_or4));
  AND_4bit and_4bit_1 (.A(A), .B(B), .AND4(and_4bit_1_and4));
  Add_4bit add_4bit_1 (.A(A), .B(B), .Sub(sub), .ADD4(add_4bit_1_add4));
  MUX4to1_4bit mux4to1_4bit_1 (
    .IN0(xor_4bit_1_xor4), .IN2(or_4bit_1_or4), .IN1(and_4bit_1_and4), .IN3(add_4bit_1_add4), .S(S),
    .MUX_out(ALU_OUT));

  // Notes on the sheet:
  //   Jacob Lamb
endmodule
